// Logisim project ex4.circ as structural Verilog: 5 circuits, main circuit RotRight
module RotRight (
  input  [15:0] INPUT0,
  input  [3:0] AMOUNT,
  output [15:0] OUTPUT0
);

  wire [3:0] not_1_out;
  wire [15:0] multiplexer_1_out, multiplexer_2_out, multiplexer_3_out, rot1_1_out_2, rot2_1_out_2,
       rot4_1_out_2, rot8_1_out_2;

  assign not_1_out = ~AMOUNT;  // NOT_Gate not_1, 4 bits wide
  rot1 rot1_1 (.in_1(INPUT0), .out_2(rot1_1_out_2));
  Multiplexer #(.width(16)) multiplexer_1 (
    .in0(rot1_1_out_2), .in1(INPUT0), .out(multiplexer_1_out), .sel(not_1_out[0]));
  rot2 rot2_1 (.in_1(multiplexer_1_out), .out_2(rot2_1_out_2));
  Multiplexer #(.width(16)) multiplexer_2 (
    .in0(rot2_1_out_2), .in1(multiplexer_1_out), .out(multiplexer_2_out), .sel(not_1_out[1]));
  rot4 rot4_1 (.in_1(multiplexer_2_out), .out_2(rot4_1_out_2));
  Multiplexer #(.width(16)) multiplexer_3 (
    .in0(rot4_1_out_2), .in1(multiplexer_2_out), .out(multiplexer_3_out), .sel(not_1_out[2]));
  rot8 rot8_1 (.in_1(multiplexer_3_out), .out_2(rot8_1_out_2));
  Multiplexer #(.width(16)) multiplexer_4 (
    .in0(rot8_1_out_2), .in1(multiplexer_3_out), .out(OUTPUT0), .sel(not_1_out[3]));

  // Other names for the same wires on the sheet: T0[15:0] = INPUT0
endmodule

module rot1 (
  input  [15:0] in_1,
  output [15:0] out_2
);


  assign out_2 = {in_1[0], in_1[15:1]};
endmodule

module rot2 (
  input  [15:0] in_1,
  output [15:0] out_2
);


  assign out_2 = {in_1[1:0], in_1[15:2]};
endmodule

module rot4 (
  input  [15:0] in_1,
  output [15:0] out_2
);


  assign out_2 = {in_1[3:0], in_1[15:4]};
endmodule

module rot8 (
  input  [15:0] in_1,
  output [15:0] out_2
);


  assign out_2 = {in_1[7:0], in_1[15:8]};
endmodule
