// Logisim project regfile.circ as structural Verilog: 1 circuit, main circuit regfile
module regfile (
  input  [4:0] ReadIndex1,
  input  [4:0] ReadIndex2,
  input  [4:0] WriteIndex,
  input  [31:0] WriteData,
  input  RegWEn,
  input  clk,
  output [31:0] ra,
  output [31:0] sp,
  output [31:0] t0,
  output [31:0] t1,
  output [31:0] t2,
  output [31:0] s0,
  output [31:0] s1,
  output [31:0] a0,
  output [31:0] ReadData1,
  output [31:0] ReadData2
);

  wire a0_we, a1_we, a2_we, a3_we, a4_we, a5_we, a6_we, a7_we, gp_we, ra_we, s0_we, s1_we, s2_we, s3_we,
       s4_we, s5_we, s6_we, s7_we, s8_we, s9_we, s10_we, s11_we, sp_we, t0_we, t1_we, t2_we, t3_we, t4_we,
       t5_we, t6_we, tp_we, x0_we;
  wire [31:0] a1, a2, a3, a4, a5, a6, a7, gp, s2, s3, s4, s5, s6, s7, s8, s9, s10, s11, t3, t4, t5, t6, tp,
       x0;

  Multiplexer #(.select(5), .width(32)) multiplexer_1 (
    .in0(x0), .in1(ra), .in2(sp), .in3(gp), .in4(tp), .in5(t0), .in6(t1), .in7(t2), .in8(s0), .in9(s1),
    .in10(a0), .in11(a1), .in12(a2), .in13(a3), .in14(a4), .in15(a5), .in16(a6), .in17(a7), .in18(s2),
    .in19(s3), .in20(s4), .in21(s5), .in22(s6), .in23(s7), .in24(s8), .in25(s9), .in26(s10), .in27(s11),
    .in28(t3), .in29(t4), .in30(t5), .in31(t6), .out(ReadData2), .sel(ReadIndex2));
  Multiplexer #(.select(5), .width(32)) multiplexer_2 (
    .in0(x0), .in1(ra), .in2(sp), .in3(gp), .in4(tp), .in5(t0), .in6(t1), .in7(t2), .in8(s0), .in9(s1),
    .in10(a0), .in11(a1), .in12(a2), .in13(a3), .in14(a4), .in15(a5), .in16(a6), .in17(a7), .in18(s2),
    .in19(s3), .in20(s4), .in21(s5), .in22(s6), .in23(s7), .in24(s8), .in25(s9), .in26(s10), .in27(s11),
    .in28(t3), .in29(t4), .in30(t5), .in31(t6), .out(ReadData1), .sel(ReadIndex1));
  Demultiplexer #(.select(5)) demultiplexer_1 (
    .out0(x0_we), .out1(ra_we), .out2(sp_we), .out3(gp_we), .out4(tp_we), .out5(t0_we), .out6(t1_we),
    .out7(t2_we), .out8(s0_we), .out9(s1_we), .out10(a0_we), .out11(a1_we), .out12(a2_we), .out13(a3_we),
    .out14(a4_we), .out15(a5_we), .out16(a6_we), .out17(a7_we), .out18(s2_we), .out19(s3_we), .out20(s4_we),
    .out21(s5_we), .out22(s6_we), .out23(s7_we), .out24(s8_we), .out25(s9_we), .out26(s10_we),
    .out27(s11_we), .out28(t3_we), .out29(t4_we), .out30(t5_we), .out31(t6_we), .in(RegWEn), .sel(WriteIndex));
  Register #(.width(32)) register_1 (.D({32{1'b0}}), .en(x0_we), .clk(clk), .Q(x0));  // open: clr
  Register #(.width(32)) register_2 (.D(WriteData), .en(ra_we), .clk(clk), .Q(ra));  // open: clr
  Register #(.width(32)) register_3 (.D(WriteData), .en(sp_we), .clk(clk), .Q(sp));  // open: clr
  Register #(.width(32)) register_4 (.D(WriteData), .en(gp_we), .clk(clk), .Q(gp));  // open: clr
  Register #(.width(32)) register_5 (.D(WriteData), .en(tp_we), .clk(clk), .Q(tp));  // open: clr
  Register #(.width(32)) register_6 (.D(WriteData), .en(t0_we), .clk(clk), .Q(t0));  // open: clr
  Register #(.width(32)) register_7 (.D(WriteData), .en(t1_we), .clk(clk), .Q(t1));  // open: clr
  Register #(.width(32)) register_8 (.D(WriteData), .en(t2_we), .clk(clk), .Q(t2));  // open: clr
  Register #(.width(32)) register_9 (.D(WriteData), .en(s0_we), .clk(clk), .Q(s0));  // open: clr
  Register #(.width(32)) register_10 (.D(WriteData), .en(s1_we), .clk(clk), .Q(s1));  // open: clr
  Register #(.width(32)) register_11 (.D(WriteData), .en(a0_we), .clk(clk), .Q(a0));  // open: clr
  Register #(.width(32)) register_12 (.D(WriteData), .en(a1_we), .clk(clk), .Q(a1));  // open: clr
  Register #(.width(32)) register_13 (.D(WriteData), .en(a2_we), .clk(clk), .Q(a2));  // open: clr
  Register #(.width(32)) register_14 (.D(WriteData), .en(a3_we), .clk(clk), .Q(a3));  // open: clr
  Register #(.width(32)) register_15 (.D(WriteData), .en(a4_we), .clk(clk), .Q(a4));  // open: clr
  Register #(.width(32)) register_16 (.D(WriteData), .en(a5_we), .clk(clk), .Q(a5));  // open: clr
  Register #(.width(32)) register_17 (.D(WriteData), .en(a6_we), .clk(clk), .Q(a6));  // open: clr
  Register #(.width(32)) register_18 (.D(WriteData), .en(a7_we), .clk(clk), .Q(a7));  // open: clr
  Register #(.width(32)) register_19 (.D(WriteData), .en(s2_we), .clk(clk), .Q(s2));  // open: clr
  Register #(.width(32)) register_20 (.D(WriteData), .en(s3_we), .clk(clk), .Q(s3));  // open: clr
  Register #(.width(32)) register_21 (.D(WriteData), .en(s4_we), .clk(clk), .Q(s4));  // open: clr
  Register #(.width(32)) register_22 (.D(WriteData), .en(s5_we), .clk(clk), .Q(s5));  // open: clr
  Register #(.width(32)) register_23 (.D(WriteData), .en(s6_we), .clk(clk), .Q(s6));  // open: clr
  Register #(.width(32)) register_24 (.D(WriteData), .en(s7_we), .clk(clk), .Q(s7));  // open: clr
  Register #(.width(32)) register_25 (.D(WriteData), .en(s8_we), .clk(clk), .Q(s8));  // open: clr
  Register #(.width(32)) register_26 (.D(WriteData), .en(s9_we), .clk(clk), .Q(s9));  // open: clr
  Register #(.width(32)) register_27 (.D(WriteData), .en(s10_we), .clk(clk), .Q(s10));  // open: clr
  Register #(.width(32)) register_28 (.D(WriteData), .en(s11_we), .clk(clk), .Q(s11));  // open: clr
  Register #(.width(32)) register_29 (.D(WriteData), .en(t3_we), .clk(clk), .Q(t3));  // open: clr
  Register #(.width(32)) register_30 (.D(WriteData), .en(t4_we), .clk(clk), .Q(t4));  // open: clr
  Register #(.width(32)) register_31 (.D(WriteData), .en(t5_we), .clk(clk), .Q(t5));  // open: clr
  Register #(.width(32)) register_32 (.D(WriteData), .en(t6_we), .clk(clk), .Q(t6));  // open: clr

  // Notes on the sheet:
  //   INPUTS to your circuit
  //   DON'T CHANGE THE LOCATIONS OF THE INPUTS AND OUTPUTS!
  //   These are DEBUG/TEST outputs from your circuit.
  //   OUTPUTS from your circuit
endmodule
